// Logisim project CPU.circ as structural Verilog
module _1_bit_m (
  input  i,
  input  s,
  output o
);

  wire _1_out, _2_out, _4_out;

  nand _1 (_1_out, i, s);
  nand _2 (_2_out, _1_out, s);
  nand _3 (o, _1_out, _4_out);
  nand _4 (_4_out, o, _2_out);
endmodule

module _8_bit_Register (
  input  i,
  input  i_2,
  input  i_3,
  input  i_4,
  input  i_5,
  input  i_6,
  input  i_7,
  input  i_8,
  input  s,
  input  e,
  output o,
  output o_2,
  output o_3,
  output o_4,
  output o_5,
  output o_6,
  output o_7,
  output o_8
);

  wire n8_bit_memory_1_o, n8_bit_memory_1_o_2, n8_bit_memory_1_o_3, n8_bit_memory_1_o_4, n8_bit_memory_1_o_5,
       n8_bit_memory_1_o_6, n8_bit_memory_1_o_7, n8_bit_memory_1_o_8;

  _8_bit_Memory u_8_bit_memory_1 (
    .o(n8_bit_memory_1_o), .o_2(n8_bit_memory_1_o_2), .o_3(n8_bit_memory_1_o_3), .o_4(n8_bit_memory_1_o_4),
    .o_5(n8_bit_memory_1_o_5), .o_6(n8_bit_memory_1_o_6), .o_7(n8_bit_memory_1_o_7),
    .o_8(n8_bit_memory_1_o_8), .i_2(i_2), .i_3(i_3), .i_4(i_4), .i_5(i_5), .i_6(i_6), .i_7(i_7), .i_8(i_8),
    .s(s), .i(i));
  _8_bit_Enabler u_8_bit_enabler_1 (
    .o_3(o_3), .o_4(o_4), .o_5(o_5), .o_6(o_6), .o_7(o_7), .o_8(o_8), .o(o), .o_2(o_2),
    .i_3(n8_bit_memory_1_o_3), .i_4(n8_bit_memory_1_o_4), .i_5(n8_bit_memory_1_o_5),
    .i_6(n8_bit_memory_1_o_6), .i_7(n8_bit_memory_1_o_7), .i(n8_bit_memory_1_o), .i_8(n8_bit_memory_1_o_8),
    .e(e), .i_2(n8_bit_memory_1_o_2));
endmodule

module _1_byte_Register (
  input  [7:0] i,
  input  s,
  input  e,
  output [7:0] o
);

  wire [7:0] n1_byte_memory_1_o;

  _1_byte_Memory u_1_byte_memory_1 (.o(n1_byte_memory_1_o), .i(i), .s(s));
  _1_byte_Enabler u_1_byte_enabler_1 (.o(o), .i(n1_byte_memory_1_o), .e(e));
endmodule

module test_Register (
  input  in_1,
  input  in_2,
  input  in_3,
  input  in_4,
  input  [7:0] in_5,
  output [7:0] out_6,
  output [7:0] out_7
);

  wire and_1_out, not_1_out, not_2_out;
  wire [7:0] controlled_buffer_1_out;

  not not_1 (not_1_out, in_4);
  not not_2 (not_2_out, in_3);
  and and_1 (and_1_out, not_1_out, not_2_out);
  assign controlled_buffer_1_out = and_1_out ? in_5 : 8'bz;  // Controlled_Buffer controlled_buffer_1
  _1_byte_Register u_1_byte_register_1 (.o(out_6), .s(in_1), .e(in_3), .i(controlled_buffer_1_out));
  assign controlled_buffer_1_out = in_3 ? out_6 : 8'bz;  // Controlled_Buffer controlled_buffer_2
  _1_byte_Register u_1_byte_register_2 (.o(out_7), .s(in_2), .e(in_4), .i(controlled_buffer_1_out));
  assign controlled_buffer_1_out = in_4 ? out_7 : 8'bz;  // Controlled_Buffer controlled_buffer_3
endmodule

module Stepper (
  input  reset,
  input  clk,
  output Step_1,
  output Step_2,
  output Step_3,
  output Step_4,
  output Step_5,
  output Step_6,
  output Step_7
);

  wire M1_o, M2_o, M3_o, M4_o, M5_o, M6_o, M7_o, M8_o, M9_o, M10_o, M11_o, not_1_out, not_2_out, not_3_out,
       not_4_out, not_5_out, not_6_out, not_7_out, not_8_out, or_1_out, or_2_out;

  not not_1 (not_1_out, clk);
  not not_2 (not_2_out, reset);
  or or_1 (or_1_out, reset, not_1_out);
  or or_2 (or_2_out, reset, clk);
  or or_3 (Step_1, reset, not_3_out);
  _1_bit_m M1 (.o(M1_o), .i(not_2_out), .s(or_1_out));
  not not_3 (not_3_out, M2_o);
  _1_bit_m M2 (.o(M2_o), .i(M1_o), .s(or_2_out));
  and and_1 (Step_2, M2_o, not_4_out);
  not not_4 (not_4_out, M4_o);
  _1_bit_m M3 (.o(M3_o), .i(M2_o), .s(or_1_out));
  and and_2 (Step_3, M4_o, not_5_out);
  _1_bit_m M4 (.o(M4_o), .i(M3_o), .s(or_2_out));
  not not_5 (not_5_out, M6_o);
  _1_bit_m M5 (.o(M5_o), .i(M4_o), .s(or_1_out));
  and and_3 (Step_4, M6_o, not_6_out);
  _1_bit_m M6 (.o(M6_o), .i(M5_o), .s(or_2_out));
  _1_bit_m M7 (.o(M7_o), .i(M6_o), .s(or_1_out));
  not not_6 (not_6_out, M8_o);
  _1_bit_m M8 (.o(M8_o), .i(M7_o), .s(or_2_out));
  and and_4 (Step_5, M8_o, not_7_out);
  _1_bit_m M9 (.o(M9_o), .i(M8_o), .s(or_1_out));
  not not_7 (not_7_out, M10_o);
  _1_bit_m M10 (.o(M10_o), .i(M9_o), .s(or_2_out));
  and and_5 (Step_6, M10_o, not_8_out);
  not not_8 (not_8_out, Step_7);
  _1_bit_m M11 (.o(M11_o), .i(M10_o), .s(or_1_out));
  _1_bit_m M12 (.o(Step_7), .i(M11_o), .s(or_2_out));
endmodule

module RAM_Register (
  input  [7:0] i,
  input  s,
  input  e,
  output [7:0] op,
  output [7:0] o
);

  _1_byte_Memory u_1_byte_memory_1 (.o(op), .i(i), .s(s));
  _1_byte_Enabler u_1_byte_enabler_1 (.o(o), .i(op), .e(e));
endmodule

module RAM_Register_Area (
  input  y,
  input  x,
  input  [7:0] bus_in,
  input  [7:0] bus_out,
  input  s,
  input  e,
  output [7:0] op
);

  wire and_1_out, and_2_out, X_out;

  and u_X (X_out, x, y);
  LED led_1 (.in(X_out));
  and and_1 (and_1_out, X_out, s);
  and and_2 (and_2_out, X_out, e);
  RAM_Register ram_register_1 (.op(op), .o(bus_out), .i(bus_in), .s(and_1_out), .e(and_2_out));
endmodule

module RAM_256 (
  input  [7:0] in_1,
  input  in_2,
  input  s,
  input  e,
  input  [7:0] in,
  output [7:0] out_6,
  output [7:0] out_7,
  output [7:0] out_8,
  output [7:0] out_9,
  output [7:0] out_10,
  output [7:0] out_11,
  output [7:0] out_12,
  output [7:0] out_13,
  output [7:0] out_14,
  output [7:0] out_15,
  output [7:0] out_16,
  output [7:0] out_17,
  output [7:0] out_18,
  output [7:0] out_19,
  output [7:0] out_20,
  output [7:0] out_21,
  output [7:0] out_22,
  output [7:0] out_23,
  output [7:0] out_24,
  output [7:0] out_25,
  output [7:0] out_26,
  output [7:0] out_27,
  output [7:0] out_28,
  output [7:0] out_29,
  output [7:0] out_30,
  output [7:0] out_31,
  output [7:0] out_32,
  output [7:0] out_33,
  output [7:0] out_34,
  output [7:0] out_35,
  output [7:0] out_36,
  output [7:0] out_37,
  output [7:0] out_38,
  output [7:0] out_39,
  output [7:0] out_40,
  output [7:0] out_41,
  output [7:0] out_42,
  output [7:0] out_43,
  output [7:0] out_44,
  output [7:0] out_45,
  output [7:0] out_46,
  output [7:0] out_47,
  output [7:0] out_48,
  output [7:0] out_49,
  output [7:0] out_50,
  output [7:0] out_51,
  output [7:0] out_52,
  output [7:0] out_53,
  output [7:0] out_54,
  output [7:0] out_55,
  output [7:0] out_56,
  output [7:0] out_57,
  output [7:0] out_58,
  output [7:0] out_59,
  output [7:0] out_60,
  output [7:0] out_61,
  output [7:0] out_62,
  output [7:0] out_63,
  output [7:0] out_64,
  output [7:0] out_65,
  output [7:0] out_66,
  output [7:0] out_67,
  output [7:0] out_68,
  output [7:0] out_69,
  output [7:0] out_70,
  output [7:0] out_71,
  output [7:0] out_72,
  output [7:0] out_73,
  output [7:0] out_74,
  output [7:0] out_75,
  output [7:0] out_76,
  output [7:0] out_77,
  output [7:0] out_78,
  output [7:0] out_79,
  output [7:0] out_80,
  output [7:0] out_81,
  output [7:0] out_82,
  output [7:0] out_83,
  output [7:0] out_84,
  output [7:0] out_85,
  output [7:0] out_86,
  output [7:0] out_87,
  output [7:0] out_88,
  output [7:0] out_89,
  output [7:0] out_90,
  output [7:0] out_91,
  output [7:0] out_92,
  output [7:0] out_93,
  output [7:0] out_94,
  output [7:0] out_95,
  output [7:0] out_96,
  output [7:0] out_97,
  output [7:0] out_98,
  output [7:0] out_99,
  output [7:0] out_100,
  output [7:0] out_101,
  output [7:0] out_102,
  output [7:0] out_103,
  output [7:0] out_104,
  output [7:0] out_105,
  output [7:0] out_106,
  output [7:0] out_107,
  output [7:0] out_108,
  output [7:0] out_109,
  output [7:0] out_110,
  output [7:0] out_111,
  output [7:0] out_112,
  output [7:0] out_113,
  output [7:0] out_114,
  output [7:0] out_115,
  output [7:0] out_116,
  output [7:0] out_117,
  output [7:0] out_118,
  output [7:0] out_119,
  output [7:0] out_120,
  output [7:0] out_121,
  output [7:0] out_122,
  output [7:0] out_123,
  output [7:0] out_124,
  output [7:0] out_125,
  output [7:0] out_126,
  output [7:0] out_127,
  output [7:0] out_128,
  output [7:0] out_129,
  output [7:0] out_130,
  output [7:0] out_131,
  output [7:0] out_132,
  output [7:0] out_133,
  output [7:0] out_134,
  output [7:0] out_135,
  output [7:0] out_136,
  output [7:0] out_137,
  output [7:0] out_138,
  output [7:0] out_139,
  output [7:0] out_140,
  output [7:0] out_141,
  output [7:0] out_142,
  output [7:0] out_143,
  output [7:0] out_144,
  output [7:0] out_145,
  output [7:0] out_146,
  output [7:0] out_147,
  output [7:0] out_148,
  output [7:0] out_149,
  output [7:0] out_150,
  output [7:0] out_151,
  output [7:0] out_152,
  output [7:0] out_153,
  output [7:0] out_154,
  output [7:0] out_155,
  output [7:0] out_156,
  output [7:0] out_157,
  output [7:0] out_158,
  output [7:0] out_159,
  output [7:0] out_160,
  output [7:0] out_161,
  output [7:0] out_162,
  output [7:0] out_163,
  output [7:0] out_164,
  output [7:0] out_165,
  output [7:0] out_166,
  output [7:0] out_167,
  output [7:0] out_168,
  output [7:0] out_169,
  output [7:0] out_170,
  output [7:0] out_171,
  output [7:0] out_172,
  output [7:0] out_173,
  output [7:0] out_174,
  output [7:0] out_175,
  output [7:0] out_176,
  output [7:0] out_177,
  output [7:0] out_178,
  output [7:0] out_179,
  output [7:0] out_180,
  output [7:0] out_181,
  output [7:0] out_182,
  output [7:0] out_183,
  output [7:0] out_184,
  output [7:0] out_185,
  output [7:0] out_186,
  output [7:0] out_187,
  output [7:0] out_188,
  output [7:0] out_189,
  output [7:0] out_190,
  output [7:0] out_191,
  output [7:0] out_192,
  output [7:0] out_193,
  output [7:0] out_194,
  output [7:0] out_195,
  output [7:0] out_196,
  output [7:0] out_197,
  output [7:0] out_198,
  output [7:0] out_199,
  output [7:0] out_200,
  output [7:0] out_201,
  output [7:0] out_202,
  output [7:0] out_203,
  output [7:0] out_204,
  output [7:0] out_205,
  output [7:0] out_206,
  output [7:0] out_207,
  output [7:0] out_208,
  output [7:0] out_209,
  output [7:0] out_210,
  output [7:0] out_211,
  output [7:0] out_212,
  output [7:0] out_213,
  output [7:0] out_214,
  output [7:0] out_215,
  output [7:0] out_216,
  output [7:0] out_217,
  output [7:0] out_218,
  output [7:0] out_219,
  output [7:0] out_220,
  output [7:0] out_221,
  output [7:0] out_222,
  output [7:0] out_223,
  output [7:0] out_224,
  output [7:0] out_225,
  output [7:0] out_226,
  output [7:0] out_227,
  output [7:0] out_228,
  output [7:0] out_229,
  output [7:0] out_230,
  output [7:0] out_231,
  output [7:0] out_232,
  output [7:0] out_233,
  output [7:0] out_234,
  output [7:0] out_235,
  output [7:0] out_236,
  output [7:0] out_237,
  output [7:0] out_238,
  output [7:0] out_239,
  output [7:0] out_240,
  output [7:0] out_241,
  output [7:0] out_242,
  output [7:0] out_243,
  output [7:0] out_244,
  output [7:0] out_245,
  output [7:0] out_246,
  output [7:0] out_247,
  output [7:0] out_248,
  output [7:0] out_249,
  output [7:0] out_250,
  output [7:0] out_251,
  output [7:0] out_252,
  output [7:0] out_253,
  output [7:0] out_254,
  output [7:0] out_255,
  output [7:0] out_256,
  output [7:0] out_257,
  output [7:0] out_258,
  output [7:0] out_259,
  output [7:0] out_260,
  output [7:0] out_261,
  output [7:0] out
);

  wire n4x16_decoder0_1_p1, n4x16_decoder0_1_p2, n4x16_decoder0_1_p3, n4x16_decoder0_1_p4,
       n4x16_decoder0_1_p5, n4x16_decoder0_1_p6, n4x16_decoder0_1_p7, n4x16_decoder0_1_p8,
       n4x16_decoder0_1_p9, n4x16_decoder0_1_p11, n4x16_decoder0_1_p13, n4x16_decoder0_1_p15,
       n4x16_decoder0_1_p17, n4x16_decoder0_1_p18, n4x16_decoder0_1_p19, n4x16_decoder0_1_p20,
       n4x16_decoder1_1_p6, n4x16_decoder1_1_p7, n4x16_decoder1_1_p8, n4x16_decoder1_1_p9,
       n4x16_decoder1_1_p10, n4x16_decoder1_1_p11, n4x16_decoder1_1_p12, n4x16_decoder1_1_p13,
       n4x16_decoder1_1_p14, n4x16_decoder1_1_p15, n4x16_decoder1_1_p16, n4x16_decoder1_1_p17,
       n4x16_decoder1_1_p18, n4x16_decoder1_1_p19, n4x16_decoder1_1_p20, n4x16_decoder1_1_p21;
  wire [7:0] n1_byte_memory_1_o;

  _1_byte_Memory u_1_byte_memory_1 (.o(n1_byte_memory_1_o), .i(in_1), .s(in_2));
  // _4x16_Decoder0 4x16_decoder0_1: pin names not known; wires that end beside it: n4x16_decoder0_1_p1, n4x16_decoder0_1_p2, n4x16_decoder0_1_p3, n4x16_decoder0_1_p4, n4x16_decoder0_1_p5, n4x16_decoder0_1_p6, n4x16_decoder0_1_p7, n4x16_decoder0_1_p8, n4x16_decoder0_1_p9, n1_byte_memory_1_o[7], n4x16_decoder0_1_p11, n1_byte_memory_1_o[6], n4x16_decoder0_1_p13, n1_byte_memory_1_o[5], n4x16_decoder0_1_p15, n1_byte_memory_1_o[4], n4x16_decoder0_1_p17, n4x16_decoder0_1_p18, n4x16_decoder0_1_p19, n4x16_decoder0_1_p20
  // _4x16_Decoder1 4x16_decoder1_1: pin names not known; wires that end beside it: n1_byte_memory_1_o[4], n1_byte_memory_1_o[0], n1_byte_memory_1_o[1], n1_byte_memory_1_o[2], n1_byte_memory_1_o[3], n4x16_decoder1_1_p6, n4x16_decoder1_1_p7, n4x16_decoder1_1_p8, n4x16_decoder1_1_p9, n4x16_decoder1_1_p10, n4x16_decoder1_1_p11, n4x16_decoder1_1_p12, n4x16_decoder1_1_p13, n4x16_decoder1_1_p14, n4x16_decoder1_1_p15, n4x16_decoder1_1_p16, n4x16_decoder1_1_p17, n4x16_decoder1_1_p18, n4x16_decoder1_1_p19, n4x16_decoder1_1_p20, n4x16_decoder1_1_p21
  RAM_Register_Area ram_register_area_1 (
    .op(out_6), .x(n4x16_decoder0_1_p20), .bus_in(in), .bus_out(out), .s(s), .e(e), .y(n4x16_decoder1_1_p21));
  RAM_Register_Area ram_register_area_2 (
    .op(out_22), .x(n4x16_decoder0_1_p19), .bus_in(in), .bus_out(out), .s(s), .e(e), .y(n4x16_decoder1_1_p21));
  RAM_Register_Area ram_register_area_3 (
    .op(out_38), .x(n4x16_decoder0_1_p18), .bus_in(in), .bus_out(out), .s(s), .e(e), .y(n4x16_decoder1_1_p21));
  RAM_Register_Area ram_register_area_4 (
    .op(out_54), .x(n4x16_decoder0_1_p17), .bus_in(in), .bus_out(out), .s(s), .e(e), .y(n4x16_decoder1_1_p21));
  RAM_Register_Area ram_register_area_5 (
    .op(out_70), .x(n4x16_decoder0_1_p15), .bus_in(in), .bus_out(out), .s(s), .e(e), .y(n4x16_decoder1_1_p21));
  RAM_Register_Area ram_register_area_6 (
    .op(out_86), .x(n4x16_decoder0_1_p13), .bus_in(in), .bus_out(out), .s(s), .e(e), .y(n4x16_decoder1_1_p21));
  RAM_Register_Area ram_register_area_7 (
    .op(out_102), .x(n4x16_decoder0_1_p11), .bus_in(in), .bus_out(out), .s(s), .e(e), .y(n4x16_decoder1_1_p21));
  RAM_Register_Area ram_register_area_8 (
    .op(out_118), .x(n4x16_decoder0_1_p9), .bus_in(in), .bus_out(out), .s(s), .e(e), .y(n4x16_decoder1_1_p21));
  RAM_Register_Area ram_register_area_9 (
    .op(out_134), .x(n4x16_decoder0_1_p8), .bus_in(in), .bus_out(out), .s(s), .e(e), .y(n4x16_decoder1_1_p21));
  RAM_Register_Area ram_register_area_10 (
    .op(out_150), .x(n4x16_decoder0_1_p7), .bus_in(in), .bus_out(out), .s(s), .e(e), .y(n4x16_decoder1_1_p21));
  RAM_Register_Area ram_register_area_11 (
    .op(out_166), .x(n4x16_decoder0_1_p6), .bus_in(in), .bus_out(out), .s(s), .e(e), .y(n4x16_decoder1_1_p21));
  RAM_Register_Area ram_register_area_12 (
    .op(out_182), .x(n4x16_decoder0_1_p5), .bus_in(in), .bus_out(out), .s(s), .e(e), .y(n4x16_decoder1_1_p21));
  RAM_Register_Area ram_register_area_13 (
    .op(out_198), .x(n4x16_decoder0_1_p4), .bus_in(in), .bus_out(out), .s(s), .e(e), .y(n4x16_decoder1_1_p21));
  RAM_Register_Area ram_register_area_14 (
    .op(out_214), .x(n4x16_decoder0_1_p3), .bus_in(in), .bus_out(out), .s(s), .e(e), .y(n4x16_decoder1_1_p21));
  RAM_Register_Area ram_register_area_15 (
    .op(out_230), .x(n4x16_decoder0_1_p2), .bus_in(in), .bus_out(out), .s(s), .e(e), .y(n4x16_decoder1_1_p21));
  RAM_Register_Area ram_register_area_16 (
    .op(out_246), .x(n4x16_decoder0_1_p1), .bus_in(in), .bus_out(out), .s(s), .e(e), .y(n4x16_decoder1_1_p21));
  RAM_Register_Area ram_register_area_17 (
    .op(out_7), .x(n4x16_decoder0_1_p20), .bus_in(in), .bus_out(out), .s(s), .e(e), .y(n4x16_decoder1_1_p20));
  RAM_Register_Area ram_register_area_18 (
    .op(out_23), .x(n4x16_decoder0_1_p19), .bus_in(in), .bus_out(out), .s(s), .e(e), .y(n4x16_decoder1_1_p20));
  RAM_Register_Area ram_register_area_19 (
    .op(out_39), .x(n4x16_decoder0_1_p18), .bus_in(in), .bus_out(out), .s(s), .e(e), .y(n4x16_decoder1_1_p20));
  RAM_Register_Area ram_register_area_20 (
    .op(out_55), .x(n4x16_decoder0_1_p17), .bus_in(in), .bus_out(out), .s(s), .e(e), .y(n4x16_decoder1_1_p20));
  RAM_Register_Area ram_register_area_21 (
    .op(out_71), .x(n4x16_decoder0_1_p15), .bus_in(in), .bus_out(out), .s(s), .e(e), .y(n4x16_decoder1_1_p20));
  RAM_Register_Area ram_register_area_22 (
    .op(out_87), .x(n4x16_decoder0_1_p13), .bus_in(in), .bus_out(out), .s(s), .e(e), .y(n4x16_decoder1_1_p20));
  RAM_Register_Area ram_register_area_23 (
    .op(out_103), .x(n4x16_decoder0_1_p11), .bus_in(in), .bus_out(out), .s(s), .e(e), .y(n4x16_decoder1_1_p20));
  RAM_Register_Area ram_register_area_24 (
    .op(out_119), .x(n4x16_decoder0_1_p9), .bus_in(in), .bus_out(out), .s(s), .e(e), .y(n4x16_decoder1_1_p20));
  RAM_Register_Area ram_register_area_25 (
    .op(out_135), .x(n4x16_decoder0_1_p8), .bus_in(in), .bus_out(out), .s(s), .e(e), .y(n4x16_decoder1_1_p20));
  RAM_Register_Area ram_register_area_26 (
    .op(out_151), .x(n4x16_decoder0_1_p7), .bus_in(in), .bus_out(out), .s(s), .e(e), .y(n4x16_decoder1_1_p20));
  RAM_Register_Area ram_register_area_27 (
    .op(out_167), .x(n4x16_decoder0_1_p6), .bus_in(in), .bus_out(out), .s(s), .e(e), .y(n4x16_decoder1_1_p20));
  RAM_Register_Area ram_register_area_28 (
    .op(out_183), .x(n4x16_decoder0_1_p5), .bus_in(in), .bus_out(out), .s(s), .e(e), .y(n4x16_decoder1_1_p20));
  RAM_Register_Area ram_register_area_29 (
    .op(out_199), .x(n4x16_decoder0_1_p4), .bus_in(in), .bus_out(out), .s(s), .e(e), .y(n4x16_decoder1_1_p20));
  RAM_Register_Area ram_register_area_30 (
    .op(out_215), .x(n4x16_decoder0_1_p3), .bus_in(in), .bus_out(out), .s(s), .e(e), .y(n4x16_decoder1_1_p20));
  RAM_Register_Area ram_register_area_31 (
    .op(out_231), .x(n4x16_decoder0_1_p2), .bus_in(in), .bus_out(out), .s(s), .e(e), .y(n4x16_decoder1_1_p20));
  RAM_Register_Area ram_register_area_32 (
    .op(out_247), .x(n4x16_decoder0_1_p1), .bus_in(in), .bus_out(out), .s(s), .e(e), .y(n4x16_decoder1_1_p20));
  RAM_Register_Area ram_register_area_33 (
    .op(out_8), .x(n4x16_decoder0_1_p20), .bus_in(in), .bus_out(out), .s(s), .e(e), .y(n4x16_decoder1_1_p19));
  RAM_Register_Area ram_register_area_34 (
    .op(out_24), .x(n4x16_decoder0_1_p19), .bus_in(in), .bus_out(out), .s(s), .e(e), .y(n4x16_decoder1_1_p19));
  RAM_Register_Area ram_register_area_35 (
    .op(out_40), .x(n4x16_decoder0_1_p18), .bus_in(in), .bus_out(out), .s(s), .e(e), .y(n4x16_decoder1_1_p19));
  RAM_Register_Area ram_register_area_36 (
    .op(out_56), .x(n4x16_decoder0_1_p17), .bus_in(in), .bus_out(out), .s(s), .e(e), .y(n4x16_decoder1_1_p19));
  RAM_Register_Area ram_register_area_37 (
    .op(out_72), .x(n4x16_decoder0_1_p15), .bus_in(in), .bus_out(out), .s(s), .e(e), .y(n4x16_decoder1_1_p19));
  RAM_Register_Area ram_register_area_38 (
    .op(out_88), .x(n4x16_decoder0_1_p13), .bus_in(in), .bus_out(out), .s(s), .e(e), .y(n4x16_decoder1_1_p19));
  RAM_Register_Area ram_register_area_39 (
    .op(out_104), .x(n4x16_decoder0_1_p11), .bus_in(in), .bus_out(out), .s(s), .e(e), .y(n4x16_decoder1_1_p19));
  RAM_Register_Area ram_register_area_40 (
    .op(out_120), .x(n4x16_decoder0_1_p9), .bus_in(in), .bus_out(out), .s(s), .e(e), .y(n4x16_decoder1_1_p19));
  RAM_Register_Area ram_register_area_41 (
    .op(out_136), .x(n4x16_decoder0_1_p8), .bus_in(in), .bus_out(out), .s(s), .e(e), .y(n4x16_decoder1_1_p19));
  RAM_Register_Area ram_register_area_42 (
    .op(out_152), .x(n4x16_decoder0_1_p7), .bus_in(in), .bus_out(out), .s(s), .e(e), .y(n4x16_decoder1_1_p19));
  RAM_Register_Area ram_register_area_43 (
    .op(out_168), .x(n4x16_decoder0_1_p6), .bus_in(in), .bus_out(out), .s(s), .e(e), .y(n4x16_decoder1_1_p19));
  RAM_Register_Area ram_register_area_44 (
    .op(out_184), .x(n4x16_decoder0_1_p5), .bus_in(in), .bus_out(out), .s(s), .e(e), .y(n4x16_decoder1_1_p19));
  RAM_Register_Area ram_register_area_45 (
    .op(out_200), .x(n4x16_decoder0_1_p4), .bus_in(in), .bus_out(out), .s(s), .e(e), .y(n4x16_decoder1_1_p19));
  RAM_Register_Area ram_register_area_46 (
    .op(out_216), .x(n4x16_decoder0_1_p3), .bus_in(in), .bus_out(out), .s(s), .e(e), .y(n4x16_decoder1_1_p19));
  RAM_Register_Area ram_register_area_47 (
    .op(out_232), .x(n4x16_decoder0_1_p2), .bus_in(in), .bus_out(out), .s(s), .e(e), .y(n4x16_decoder1_1_p19));
  RAM_Register_Area ram_register_area_48 (
    .op(out_248), .x(n4x16_decoder0_1_p1), .bus_in(in), .bus_out(out), .s(s), .e(e), .y(n4x16_decoder1_1_p19));
  RAM_Register_Area ram_register_area_49 (
    .op(out_9), .x(n4x16_decoder0_1_p20), .bus_in(in), .bus_out(out), .s(s), .e(e), .y(n4x16_decoder1_1_p18));
  RAM_Register_Area ram_register_area_50 (
    .op(out_25), .x(n4x16_decoder0_1_p19), .bus_in(in), .bus_out(out), .s(s), .e(e), .y(n4x16_decoder1_1_p18));
  RAM_Register_Area ram_register_area_51 (
    .op(out_41), .x(n4x16_decoder0_1_p18), .bus_in(in), .bus_out(out), .s(s), .e(e), .y(n4x16_decoder1_1_p18));
  RAM_Register_Area ram_register_area_52 (
    .op(out_57), .x(n4x16_decoder0_1_p17), .bus_in(in), .bus_out(out), .s(s), .e(e), .y(n4x16_decoder1_1_p18));
  RAM_Register_Area ram_register_area_53 (
    .op(out_73), .x(n4x16_decoder0_1_p15), .bus_in(in), .bus_out(out), .s(s), .e(e), .y(n4x16_decoder1_1_p18));
  RAM_Register_Area ram_register_area_54 (
    .op(out_89), .x(n4x16_decoder0_1_p13), .bus_in(in), .bus_out(out), .s(s), .e(e), .y(n4x16_decoder1_1_p18));
  RAM_Register_Area ram_register_area_55 (
    .op(out_105), .x(n4x16_decoder0_1_p11), .bus_in(in), .bus_out(out), .s(s), .e(e), .y(n4x16_decoder1_1_p18));
  RAM_Register_Area ram_register_area_56 (
    .op(out_121), .x(n4x16_decoder0_1_p9), .bus_in(in), .bus_out(out), .s(s), .e(e), .y(n4x16_decoder1_1_p18));
  RAM_Register_Area ram_register_area_57 (
    .op(out_137), .x(n4x16_decoder0_1_p8), .bus_in(in), .bus_out(out), .s(s), .e(e), .y(n4x16_decoder1_1_p18));
  RAM_Register_Area ram_register_area_58 (
    .op(out_153), .x(n4x16_decoder0_1_p7), .bus_in(in), .bus_out(out), .s(s), .e(e), .y(n4x16_decoder1_1_p18));
  RAM_Register_Area ram_register_area_59 (
    .op(out_169), .x(n4x16_decoder0_1_p6), .bus_in(in), .bus_out(out), .s(s), .e(e), .y(n4x16_decoder1_1_p18));
  RAM_Register_Area ram_register_area_60 (
    .op(out_185), .x(n4x16_decoder0_1_p5), .bus_in(in), .bus_out(out), .s(s), .e(e), .y(n4x16_decoder1_1_p18));
  RAM_Register_Area ram_register_area_61 (
    .op(out_201), .x(n4x16_decoder0_1_p4), .bus_in(in), .bus_out(out), .s(s), .e(e), .y(n4x16_decoder1_1_p18));
  RAM_Register_Area ram_register_area_62 (
    .op(out_217), .x(n4x16_decoder0_1_p3), .bus_in(in), .bus_out(out), .s(s), .e(e), .y(n4x16_decoder1_1_p18));
  RAM_Register_Area ram_register_area_63 (
    .op(out_233), .x(n4x16_decoder0_1_p2), .bus_in(in), .bus_out(out), .s(s), .e(e), .y(n4x16_decoder1_1_p18));
  RAM_Register_Area ram_register_area_64 (
    .op(out_249), .x(n4x16_decoder0_1_p1), .bus_in(in), .bus_out(out), .s(s), .e(e), .y(n4x16_decoder1_1_p18));
  RAM_Register_Area ram_register_area_65 (
    .op(out_10), .x(n4x16_decoder0_1_p20), .bus_in(in), .bus_out(out), .s(s), .e(e), .y(n4x16_decoder1_1_p17));
  RAM_Register_Area ram_register_area_66 (
    .op(out_26), .x(n4x16_decoder0_1_p19), .bus_in(in), .bus_out(out), .s(s), .e(e), .y(n4x16_decoder1_1_p17));
  RAM_Register_Area ram_register_area_67 (
    .op(out_42), .x(n4x16_decoder0_1_p18), .bus_in(in), .bus_out(out), .s(s), .e(e), .y(n4x16_decoder1_1_p17));
  RAM_Register_Area ram_register_area_68 (
    .op(out_58), .x(n4x16_decoder0_1_p17), .bus_in(in), .bus_out(out), .s(s), .e(e), .y(n4x16_decoder1_1_p17));
  RAM_Register_Area ram_register_area_69 (
    .op(out_74), .x(n4x16_decoder0_1_p15), .bus_in(in), .bus_out(out), .s(s), .e(e), .y(n4x16_decoder1_1_p17));
  RAM_Register_Area ram_register_area_70 (
    .op(out_90), .x(n4x16_decoder0_1_p13), .bus_in(in), .bus_out(out), .s(s), .e(e), .y(n4x16_decoder1_1_p17));
  RAM_Register_Area ram_register_area_71 (
    .op(out_106), .x(n4x16_decoder0_1_p11), .bus_in(in), .bus_out(out), .s(s), .e(e), .y(n4x16_decoder1_1_p17));
  RAM_Register_Area ram_register_area_72 (
    .op(out_122), .x(n4x16_decoder0_1_p9), .bus_in(in), .bus_out(out), .s(s), .e(e), .y(n4x16_decoder1_1_p17));
  RAM_Register_Area ram_register_area_73 (
    .op(out_138), .x(n4x16_decoder0_1_p8), .bus_in(in), .bus_out(out), .s(s), .e(e), .y(n4x16_decoder1_1_p17));
  RAM_Register_Area ram_register_area_74 (
    .op(out_154), .x(n4x16_decoder0_1_p7), .bus_in(in), .bus_out(out), .s(s), .e(e), .y(n4x16_decoder1_1_p17));
  RAM_Register_Area ram_register_area_75 (
    .op(out_170), .x(n4x16_decoder0_1_p6), .bus_in(in), .bus_out(out), .s(s), .e(e), .y(n4x16_decoder1_1_p17));
  RAM_Register_Area ram_register_area_76 (
    .op(out_186), .x(n4x16_decoder0_1_p5), .bus_in(in), .bus_out(out), .s(s), .e(e), .y(n4x16_decoder1_1_p17));
  RAM_Register_Area ram_register_area_77 (
    .op(out_202), .x(n4x16_decoder0_1_p4), .bus_in(in), .bus_out(out), .s(s), .e(e), .y(n4x16_decoder1_1_p17));
  RAM_Register_Area ram_register_area_78 (
    .op(out_218), .x(n4x16_decoder0_1_p3), .bus_in(in), .bus_out(out), .s(s), .e(e), .y(n4x16_decoder1_1_p17));
  RAM_Register_Area ram_register_area_79 (
    .op(out_234), .x(n4x16_decoder0_1_p2), .bus_in(in), .bus_out(out), .s(s), .e(e), .y(n4x16_decoder1_1_p17));
  RAM_Register_Area ram_register_area_80 (
    .op(out_250), .x(n4x16_decoder0_1_p1), .bus_in(in), .bus_out(out), .s(s), .e(e), .y(n4x16_decoder1_1_p17));
  RAM_Register_Area ram_register_area_81 (
    .op(out_11), .x(n4x16_decoder0_1_p20), .bus_in(in), .bus_out(out), .s(s), .e(e), .y(n4x16_decoder1_1_p16));
  RAM_Register_Area ram_register_area_82 (
    .op(out_27), .x(n4x16_decoder0_1_p19), .bus_in(in), .bus_out(out), .s(s), .e(e), .y(n4x16_decoder1_1_p16));
  RAM_Register_Area ram_register_area_83 (
    .op(out_43), .x(n4x16_decoder0_1_p18), .bus_in(in), .bus_out(out), .s(s), .e(e), .y(n4x16_decoder1_1_p16));
  RAM_Register_Area ram_register_area_84 (
    .op(out_59), .x(n4x16_decoder0_1_p17), .bus_in(in), .bus_out(out), .s(s), .e(e), .y(n4x16_decoder1_1_p16));
  RAM_Register_Area ram_register_area_85 (
    .op(out_75), .x(n4x16_decoder0_1_p15), .bus_in(in), .bus_out(out), .s(s), .e(e), .y(n4x16_decoder1_1_p16));
  RAM_Register_Area ram_register_area_86 (
    .op(out_91), .x(n4x16_decoder0_1_p13), .bus_in(in), .bus_out(out), .s(s), .e(e), .y(n4x16_decoder1_1_p16));
  RAM_Register_Area ram_register_area_87 (
    .op(out_107), .x(n4x16_decoder0_1_p11), .bus_in(in), .bus_out(out), .s(s), .e(e), .y(n4x16_decoder1_1_p16));
  RAM_Register_Area ram_register_area_88 (
    .op(out_123), .x(n4x16_decoder0_1_p9), .bus_in(in), .bus_out(out), .s(s), .e(e), .y(n4x16_decoder1_1_p16));
  RAM_Register_Area ram_register_area_89 (
    .op(out_139), .x(n4x16_decoder0_1_p8), .bus_in(in), .bus_out(out), .s(s), .e(e), .y(n4x16_decoder1_1_p16));
  RAM_Register_Area ram_register_area_90 (
    .op(out_155), .x(n4x16_decoder0_1_p7), .bus_in(in), .bus_out(out), .s(s), .e(e), .y(n4x16_decoder1_1_p16));
  RAM_Register_Area ram_register_area_91 (
    .op(out_171), .x(n4x16_decoder0_1_p6), .bus_in(in), .bus_out(out), .s(s), .e(e), .y(n4x16_decoder1_1_p16));
  RAM_Register_Area ram_register_area_92 (
    .op(out_187), .x(n4x16_decoder0_1_p5), .bus_in(in), .bus_out(out), .s(s), .e(e), .y(n4x16_decoder1_1_p16));
  RAM_Register_Area ram_register_area_93 (
    .op(out_203), .x(n4x16_decoder0_1_p4), .bus_in(in), .bus_out(out), .s(s), .e(e), .y(n4x16_decoder1_1_p16));
  RAM_Register_Area ram_register_area_94 (
    .op(out_219), .x(n4x16_decoder0_1_p3), .bus_in(in), .bus_out(out), .s(s), .e(e), .y(n4x16_decoder1_1_p16));
  RAM_Register_Area ram_register_area_95 (
    .op(out_235), .x(n4x16_decoder0_1_p2), .bus_in(in), .bus_out(out), .s(s), .e(e), .y(n4x16_decoder1_1_p16));
  RAM_Register_Area ram_register_area_96 (
    .op(out_251), .x(n4x16_decoder0_1_p1), .bus_in(in), .bus_out(out), .s(s), .e(e), .y(n4x16_decoder1_1_p16));
  RAM_Register_Area ram_register_area_97 (
    .op(out_12), .x(n4x16_decoder0_1_p20), .bus_in(in), .bus_out(out), .s(s), .e(e), .y(n4x16_decoder1_1_p15));
  RAM_Register_Area ram_register_area_98 (
    .op(out_28), .x(n4x16_decoder0_1_p19), .bus_in(in), .bus_out(out), .s(s), .e(e), .y(n4x16_decoder1_1_p15));
  RAM_Register_Area ram_register_area_99 (
    .op(out_44), .x(n4x16_decoder0_1_p18), .bus_in(in), .bus_out(out), .s(s), .e(e), .y(n4x16_decoder1_1_p15));
  RAM_Register_Area ram_register_area_100 (
    .op(out_60), .x(n4x16_decoder0_1_p17), .bus_in(in), .bus_out(out), .s(s), .e(e), .y(n4x16_decoder1_1_p15));
  RAM_Register_Area ram_register_area_101 (
    .op(out_76), .x(n4x16_decoder0_1_p15), .bus_in(in), .bus_out(out), .s(s), .e(e), .y(n4x16_decoder1_1_p15));
  RAM_Register_Area ram_register_area_102 (
    .op(out_92), .x(n4x16_decoder0_1_p13), .bus_in(in), .bus_out(out), .s(s), .e(e), .y(n4x16_decoder1_1_p15));
  RAM_Register_Area ram_register_area_103 (
    .op(out_108), .x(n4x16_decoder0_1_p11), .bus_in(in), .bus_out(out), .s(s), .e(e), .y(n4x16_decoder1_1_p15));
  RAM_Register_Area ram_register_area_104 (
    .op(out_124), .x(n4x16_decoder0_1_p9), .bus_in(in), .bus_out(out), .s(s), .e(e), .y(n4x16_decoder1_1_p15));
  RAM_Register_Area ram_register_area_105 (
    .op(out_140), .x(n4x16_decoder0_1_p8), .bus_in(in), .bus_out(out), .s(s), .e(e), .y(n4x16_decoder1_1_p15));
  RAM_Register_Area ram_register_area_106 (
    .op(out_156), .x(n4x16_decoder0_1_p7), .bus_in(in), .bus_out(out), .s(s), .e(e), .y(n4x16_decoder1_1_p15));
  RAM_Register_Area ram_register_area_107 (
    .op(out_172), .x(n4x16_decoder0_1_p6), .bus_in(in), .bus_out(out), .s(s), .e(e), .y(n4x16_decoder1_1_p15));
  RAM_Register_Area ram_register_area_108 (
    .op(out_188), .x(n4x16_decoder0_1_p5), .bus_in(in), .bus_out(out), .s(s), .e(e), .y(n4x16_decoder1_1_p15));
  RAM_Register_Area ram_register_area_109 (
    .op(out_204), .x(n4x16_decoder0_1_p4), .bus_in(in), .bus_out(out), .s(s), .e(e), .y(n4x16_decoder1_1_p15));
  RAM_Register_Area ram_register_area_110 (
    .op(out_220), .x(n4x16_decoder0_1_p3), .bus_in(in), .bus_out(out), .s(s), .e(e), .y(n4x16_decoder1_1_p15));
  RAM_Register_Area ram_register_area_111 (
    .op(out_236), .x(n4x16_decoder0_1_p2), .bus_in(in), .bus_out(out), .s(s), .e(e), .y(n4x16_decoder1_1_p15));
  RAM_Register_Area ram_register_area_112 (
    .op(out_252), .x(n4x16_decoder0_1_p1), .bus_in(in), .bus_out(out), .s(s), .e(e), .y(n4x16_decoder1_1_p15));
  RAM_Register_Area ram_register_area_113 (
    .op(out_13), .x(n4x16_decoder0_1_p20), .bus_in(in), .bus_out(out), .s(s), .e(e), .y(n4x16_decoder1_1_p14));
  RAM_Register_Area ram_register_area_114 (
    .op(out_29), .x(n4x16_decoder0_1_p19), .bus_in(in), .bus_out(out), .s(s), .e(e), .y(n4x16_decoder1_1_p14));
  RAM_Register_Area ram_register_area_115 (
    .op(out_45), .x(n4x16_decoder0_1_p18), .bus_in(in), .bus_out(out), .s(s), .e(e), .y(n4x16_decoder1_1_p14));
  RAM_Register_Area ram_register_area_116 (
    .op(out_61), .x(n4x16_decoder0_1_p17), .bus_in(in), .bus_out(out), .s(s), .e(e), .y(n4x16_decoder1_1_p14));
  RAM_Register_Area ram_register_area_117 (
    .op(out_77), .x(n4x16_decoder0_1_p15), .bus_in(in), .bus_out(out), .s(s), .e(e), .y(n4x16_decoder1_1_p14));
  RAM_Register_Area ram_register_area_118 (
    .op(out_93), .x(n4x16_decoder0_1_p13), .bus_in(in), .bus_out(out), .s(s), .e(e), .y(n4x16_decoder1_1_p14));
  RAM_Register_Area ram_register_area_119 (
    .op(out_109), .x(n4x16_decoder0_1_p11), .bus_in(in), .bus_out(out), .s(s), .e(e), .y(n4x16_decoder1_1_p14));
  RAM_Register_Area ram_register_area_120 (
    .op(out_125), .x(n4x16_decoder0_1_p9), .bus_in(in), .bus_out(out), .s(s), .e(e), .y(n4x16_decoder1_1_p14));
  RAM_Register_Area ram_register_area_121 (
    .op(out_141), .x(n4x16_decoder0_1_p8), .bus_in(in), .bus_out(out), .s(s), .e(e), .y(n4x16_decoder1_1_p14));
  RAM_Register_Area ram_register_area_122 (
    .op(out_157), .x(n4x16_decoder0_1_p7), .bus_in(in), .bus_out(out), .s(s), .e(e), .y(n4x16_decoder1_1_p14));
  RAM_Register_Area ram_register_area_123 (
    .op(out_173), .x(n4x16_decoder0_1_p6), .bus_in(in), .bus_out(out), .s(s), .e(e), .y(n4x16_decoder1_1_p14));
  RAM_Register_Area ram_register_area_124 (
    .op(out_189), .x(n4x16_decoder0_1_p5), .bus_in(in), .bus_out(out), .s(s), .e(e), .y(n4x16_decoder1_1_p14));
  RAM_Register_Area ram_register_area_125 (
    .op(out_205), .x(n4x16_decoder0_1_p4), .bus_in(in), .bus_out(out), .s(s), .e(e), .y(n4x16_decoder1_1_p14));
  RAM_Register_Area ram_register_area_126 (
    .op(out_221), .x(n4x16_decoder0_1_p3), .bus_in(in), .bus_out(out), .s(s), .e(e), .y(n4x16_decoder1_1_p14));
  RAM_Register_Area ram_register_area_127 (
    .op(out_237), .x(n4x16_decoder0_1_p2), .bus_in(in), .bus_out(out), .s(s), .e(e), .y(n4x16_decoder1_1_p14));
  RAM_Register_Area ram_register_area_128 (
    .op(out_253), .x(n4x16_decoder0_1_p1), .bus_in(in), .bus_out(out), .s(s), .e(e), .y(n4x16_decoder1_1_p14));
  RAM_Register_Area ram_register_area_129 (
    .op(out_14), .x(n4x16_decoder0_1_p20), .bus_in(in), .bus_out(out), .s(s), .e(e), .y(n4x16_decoder1_1_p13));
  RAM_Register_Area ram_register_area_130 (
    .op(out_30), .x(n4x16_decoder0_1_p19), .bus_in(in), .bus_out(out), .s(s), .e(e), .y(n4x16_decoder1_1_p13));
  RAM_Register_Area ram_register_area_131 (
    .op(out_46), .x(n4x16_decoder0_1_p18), .bus_in(in), .bus_out(out), .s(s), .e(e), .y(n4x16_decoder1_1_p13));
  RAM_Register_Area ram_register_area_132 (
    .op(out_62), .x(n4x16_decoder0_1_p17), .bus_in(in), .bus_out(out), .s(s), .e(e), .y(n4x16_decoder1_1_p13));
  RAM_Register_Area ram_register_area_133 (
    .op(out_78), .x(n4x16_decoder0_1_p15), .bus_in(in), .bus_out(out), .s(s), .e(e), .y(n4x16_decoder1_1_p13));
  RAM_Register_Area ram_register_area_134 (
    .op(out_94), .x(n4x16_decoder0_1_p13), .bus_in(in), .bus_out(out), .s(s), .e(e), .y(n4x16_decoder1_1_p13));
  RAM_Register_Area ram_register_area_135 (
    .op(out_110), .x(n4x16_decoder0_1_p11), .bus_in(in), .bus_out(out), .s(s), .e(e), .y(n4x16_decoder1_1_p13));
  RAM_Register_Area ram_register_area_136 (
    .op(out_126), .x(n4x16_decoder0_1_p9), .bus_in(in), .bus_out(out), .s(s), .e(e), .y(n4x16_decoder1_1_p13));
  RAM_Register_Area ram_register_area_137 (
    .op(out_142), .x(n4x16_decoder0_1_p8), .bus_in(in), .bus_out(out), .s(s), .e(e), .y(n4x16_decoder1_1_p13));
  RAM_Register_Area ram_register_area_138 (
    .op(out_158), .x(n4x16_decoder0_1_p7), .bus_in(in), .bus_out(out), .s(s), .e(e), .y(n4x16_decoder1_1_p13));
  RAM_Register_Area ram_register_area_139 (
    .op(out_174), .x(n4x16_decoder0_1_p6), .bus_in(in), .bus_out(out), .s(s), .e(e), .y(n4x16_decoder1_1_p13));
  RAM_Register_Area ram_register_area_140 (
    .op(out_190), .x(n4x16_decoder0_1_p5), .bus_in(in), .bus_out(out), .s(s), .e(e), .y(n4x16_decoder1_1_p13));
  RAM_Register_Area ram_register_area_141 (
    .op(out_206), .x(n4x16_decoder0_1_p4), .bus_in(in), .bus_out(out), .s(s), .e(e), .y(n4x16_decoder1_1_p13));
  RAM_Register_Area ram_register_area_142 (
    .op(out_222), .x(n4x16_decoder0_1_p3), .bus_in(in), .bus_out(out), .s(s), .e(e), .y(n4x16_decoder1_1_p13));
  RAM_Register_Area ram_register_area_143 (
    .op(out_238), .x(n4x16_decoder0_1_p2), .bus_in(in), .bus_out(out), .s(s), .e(e), .y(n4x16_decoder1_1_p13));
  RAM_Register_Area ram_register_area_144 (
    .op(out_254), .x(n4x16_decoder0_1_p1), .bus_in(in), .bus_out(out), .s(s), .e(e), .y(n4x16_decoder1_1_p13));
  RAM_Register_Area ram_register_area_145 (
    .op(out_15), .x(n4x16_decoder0_1_p20), .bus_in(in), .bus_out(out), .s(s), .e(e), .y(n4x16_decoder1_1_p12));
  RAM_Register_Area ram_register_area_146 (
    .op(out_31), .x(n4x16_decoder0_1_p19), .bus_in(in), .bus_out(out), .s(s), .e(e), .y(n4x16_decoder1_1_p12));
  RAM_Register_Area ram_register_area_147 (
    .op(out_47), .x(n4x16_decoder0_1_p18), .bus_in(in), .bus_out(out), .s(s), .e(e), .y(n4x16_decoder1_1_p12));
  RAM_Register_Area ram_register_area_148 (
    .op(out_63), .x(n4x16_decoder0_1_p17), .bus_in(in), .bus_out(out), .s(s), .e(e), .y(n4x16_decoder1_1_p12));
  RAM_Register_Area ram_register_area_149 (
    .op(out_79), .x(n4x16_decoder0_1_p15), .bus_in(in), .bus_out(out), .s(s), .e(e), .y(n4x16_decoder1_1_p12));
  RAM_Register_Area ram_register_area_150 (
    .op(out_95), .x(n4x16_decoder0_1_p13), .bus_in(in), .bus_out(out), .s(s), .e(e), .y(n4x16_decoder1_1_p12));
  RAM_Register_Area ram_register_area_151 (
    .op(out_111), .x(n4x16_decoder0_1_p11), .bus_in(in), .bus_out(out), .s(s), .e(e), .y(n4x16_decoder1_1_p12));
  RAM_Register_Area ram_register_area_152 (
    .op(out_127), .x(n4x16_decoder0_1_p9), .bus_in(in), .bus_out(out), .s(s), .e(e), .y(n4x16_decoder1_1_p12));
  RAM_Register_Area ram_register_area_153 (
    .op(out_143), .x(n4x16_decoder0_1_p8), .bus_in(in), .bus_out(out), .s(s), .e(e), .y(n4x16_decoder1_1_p12));
  RAM_Register_Area ram_register_area_154 (
    .op(out_159), .x(n4x16_decoder0_1_p7), .bus_in(in), .bus_out(out), .s(s), .e(e), .y(n4x16_decoder1_1_p12));
  RAM_Register_Area ram_register_area_155 (
    .op(out_175), .x(n4x16_decoder0_1_p6), .bus_in(in), .bus_out(out), .s(s), .e(e), .y(n4x16_decoder1_1_p12));
  RAM_Register_Area ram_register_area_156 (
    .op(out_191), .x(n4x16_decoder0_1_p5), .bus_in(in), .bus_out(out), .s(s), .e(e), .y(n4x16_decoder1_1_p12));
  RAM_Register_Area ram_register_area_157 (
    .op(out_207), .x(n4x16_decoder0_1_p4), .bus_in(in), .bus_out(out), .s(s), .e(e), .y(n4x16_decoder1_1_p12));
  RAM_Register_Area ram_register_area_158 (
    .op(out_223), .x(n4x16_decoder0_1_p3), .bus_in(in), .bus_out(out), .s(s), .e(e), .y(n4x16_decoder1_1_p12));
  RAM_Register_Area ram_register_area_159 (
    .op(out_239), .x(n4x16_decoder0_1_p2), .bus_in(in), .bus_out(out), .s(s), .e(e), .y(n4x16_decoder1_1_p12));
  RAM_Register_Area ram_register_area_160 (
    .op(out_255), .x(n4x16_decoder0_1_p1), .bus_in(in), .bus_out(out), .s(s), .e(e), .y(n4x16_decoder1_1_p12));
  RAM_Register_Area ram_register_area_161 (
    .op(out_16), .x(n4x16_decoder0_1_p20), .bus_in(in), .bus_out(out), .s(s), .e(e), .y(n4x16_decoder1_1_p11));
  RAM_Register_Area ram_register_area_162 (
    .op(out_32), .x(n4x16_decoder0_1_p19), .bus_in(in), .bus_out(out), .s(s), .e(e), .y(n4x16_decoder1_1_p11));
  RAM_Register_Area ram_register_area_163 (
    .op(out_48), .x(n4x16_decoder0_1_p18), .bus_in(in), .bus_out(out), .s(s), .e(e), .y(n4x16_decoder1_1_p11));
  RAM_Register_Area ram_register_area_164 (
    .op(out_64), .x(n4x16_decoder0_1_p17), .bus_in(in), .bus_out(out), .s(s), .e(e), .y(n4x16_decoder1_1_p11));
  RAM_Register_Area ram_register_area_165 (
    .op(out_80), .x(n4x16_decoder0_1_p15), .bus_in(in), .bus_out(out), .s(s), .e(e), .y(n4x16_decoder1_1_p11));
  RAM_Register_Area ram_register_area_166 (
    .op(out_96), .x(n4x16_decoder0_1_p13), .bus_in(in), .bus_out(out), .s(s), .e(e), .y(n4x16_decoder1_1_p11));
  RAM_Register_Area ram_register_area_167 (
    .op(out_112), .x(n4x16_decoder0_1_p11), .bus_in(in), .bus_out(out), .s(s), .e(e), .y(n4x16_decoder1_1_p11));
  RAM_Register_Area ram_register_area_168 (
    .op(out_128), .x(n4x16_decoder0_1_p9), .bus_in(in), .bus_out(out), .s(s), .e(e), .y(n4x16_decoder1_1_p11));
  RAM_Register_Area ram_register_area_169 (
    .op(out_144), .x(n4x16_decoder0_1_p8), .bus_in(in), .bus_out(out), .s(s), .e(e), .y(n4x16_decoder1_1_p11));
  RAM_Register_Area ram_register_area_170 (
    .op(out_160), .x(n4x16_decoder0_1_p7), .bus_in(in), .bus_out(out), .s(s), .e(e), .y(n4x16_decoder1_1_p11));
  RAM_Register_Area ram_register_area_171 (
    .op(out_176), .x(n4x16_decoder0_1_p6), .bus_in(in), .bus_out(out), .s(s), .e(e), .y(n4x16_decoder1_1_p11));
  RAM_Register_Area ram_register_area_172 (
    .op(out_192), .x(n4x16_decoder0_1_p5), .bus_in(in), .bus_out(out), .s(s), .e(e), .y(n4x16_decoder1_1_p11));
  RAM_Register_Area ram_register_area_173 (
    .op(out_208), .x(n4x16_decoder0_1_p4), .bus_in(in), .bus_out(out), .s(s), .e(e), .y(n4x16_decoder1_1_p11));
  RAM_Register_Area ram_register_area_174 (
    .op(out_224), .x(n4x16_decoder0_1_p3), .bus_in(in), .bus_out(out), .s(s), .e(e), .y(n4x16_decoder1_1_p11));
  RAM_Register_Area ram_register_area_175 (
    .op(out_240), .x(n4x16_decoder0_1_p2), .bus_in(in), .bus_out(out), .s(s), .e(e), .y(n4x16_decoder1_1_p11));
  RAM_Register_Area ram_register_area_176 (
    .op(out_256), .x(n4x16_decoder0_1_p1), .bus_in(in), .bus_out(out), .s(s), .e(e), .y(n4x16_decoder1_1_p11));
  RAM_Register_Area ram_register_area_177 (
    .op(out_17), .x(n4x16_decoder0_1_p20), .bus_in(in), .bus_out(out), .s(s), .e(e), .y(n4x16_decoder1_1_p10));
  RAM_Register_Area ram_register_area_178 (
    .op(out_33), .x(n4x16_decoder0_1_p19), .bus_in(in), .bus_out(out), .s(s), .e(e), .y(n4x16_decoder1_1_p10));
  RAM_Register_Area ram_register_area_179 (
    .op(out_49), .x(n4x16_decoder0_1_p18), .bus_in(in), .bus_out(out), .s(s), .e(e), .y(n4x16_decoder1_1_p10));
  RAM_Register_Area ram_register_area_180 (
    .op(out_65), .x(n4x16_decoder0_1_p17), .bus_in(in), .bus_out(out), .s(s), .e(e), .y(n4x16_decoder1_1_p10));
  RAM_Register_Area ram_register_area_181 (
    .op(out_81), .x(n4x16_decoder0_1_p15), .bus_in(in), .bus_out(out), .s(s), .e(e), .y(n4x16_decoder1_1_p10));
  RAM_Register_Area ram_register_area_182 (
    .op(out_97), .x(n4x16_decoder0_1_p13), .bus_in(in), .bus_out(out), .s(s), .e(e), .y(n4x16_decoder1_1_p10));
  RAM_Register_Area ram_register_area_183 (
    .op(out_113), .x(n4x16_decoder0_1_p11), .bus_in(in), .bus_out(out), .s(s), .e(e), .y(n4x16_decoder1_1_p10));
  RAM_Register_Area ram_register_area_184 (
    .op(out_129), .x(n4x16_decoder0_1_p9), .bus_in(in), .bus_out(out), .s(s), .e(e), .y(n4x16_decoder1_1_p10));
  RAM_Register_Area ram_register_area_185 (
    .op(out_145), .x(n4x16_decoder0_1_p8), .bus_in(in), .bus_out(out), .s(s), .e(e), .y(n4x16_decoder1_1_p10));
  RAM_Register_Area ram_register_area_186 (
    .op(out_161), .x(n4x16_decoder0_1_p7), .bus_in(in), .bus_out(out), .s(s), .e(e), .y(n4x16_decoder1_1_p10));
  RAM_Register_Area ram_register_area_187 (
    .op(out_177), .x(n4x16_decoder0_1_p6), .bus_in(in), .bus_out(out), .s(s), .e(e), .y(n4x16_decoder1_1_p10));
  RAM_Register_Area ram_register_area_188 (
    .op(out_193), .x(n4x16_decoder0_1_p5), .bus_in(in), .bus_out(out), .s(s), .e(e), .y(n4x16_decoder1_1_p10));
  RAM_Register_Area ram_register_area_189 (
    .op(out_209), .x(n4x16_decoder0_1_p4), .bus_in(in), .bus_out(out), .s(s), .e(e), .y(n4x16_decoder1_1_p10));
  RAM_Register_Area ram_register_area_190 (
    .op(out_225), .x(n4x16_decoder0_1_p3), .bus_in(in), .bus_out(out), .s(s), .e(e), .y(n4x16_decoder1_1_p10));
  RAM_Register_Area ram_register_area_191 (
    .op(out_241), .x(n4x16_decoder0_1_p2), .bus_in(in), .bus_out(out), .s(s), .e(e), .y(n4x16_decoder1_1_p10));
  RAM_Register_Area ram_register_area_192 (
    .op(out_257), .x(n4x16_decoder0_1_p1), .bus_in(in), .bus_out(out), .s(s), .e(e), .y(n4x16_decoder1_1_p10));
  RAM_Register_Area ram_register_area_193 (
    .op(out_18), .x(n4x16_decoder0_1_p20), .bus_in(in), .bus_out(out), .s(s), .e(e), .y(n4x16_decoder1_1_p9));
  RAM_Register_Area ram_register_area_194 (
    .op(out_34), .x(n4x16_decoder0_1_p19), .bus_in(in), .bus_out(out), .s(s), .e(e), .y(n4x16_decoder1_1_p9));
  RAM_Register_Area ram_register_area_195 (
    .op(out_50), .x(n4x16_decoder0_1_p18), .bus_in(in), .bus_out(out), .s(s), .e(e), .y(n4x16_decoder1_1_p9));
  RAM_Register_Area ram_register_area_196 (
    .op(out_66), .x(n4x16_decoder0_1_p17), .bus_in(in), .bus_out(out), .s(s), .e(e), .y(n4x16_decoder1_1_p9));
  RAM_Register_Area ram_register_area_197 (
    .op(out_82), .x(n4x16_decoder0_1_p15), .bus_in(in), .bus_out(out), .s(s), .e(e), .y(n4x16_decoder1_1_p9));
  RAM_Register_Area ram_register_area_198 (
    .op(out_98), .x(n4x16_decoder0_1_p13), .bus_in(in), .bus_out(out), .s(s), .e(e), .y(n4x16_decoder1_1_p9));
  RAM_Register_Area ram_register_area_199 (
    .op(out_114), .x(n4x16_decoder0_1_p11), .bus_in(in), .bus_out(out), .s(s), .e(e), .y(n4x16_decoder1_1_p9));
  RAM_Register_Area ram_register_area_200 (
    .op(out_130), .x(n4x16_decoder0_1_p9), .bus_in(in), .bus_out(out), .s(s), .e(e), .y(n4x16_decoder1_1_p9));
  RAM_Register_Area ram_register_area_201 (
    .op(out_146), .x(n4x16_decoder0_1_p8), .bus_in(in), .bus_out(out), .s(s), .e(e), .y(n4x16_decoder1_1_p9));
  RAM_Register_Area ram_register_area_202 (
    .op(out_162), .x(n4x16_decoder0_1_p7), .bus_in(in), .bus_out(out), .s(s), .e(e), .y(n4x16_decoder1_1_p9));
  RAM_Register_Area ram_register_area_203 (
    .op(out_178), .x(n4x16_decoder0_1_p6), .bus_in(in), .bus_out(out), .s(s), .e(e), .y(n4x16_decoder1_1_p9));
  RAM_Register_Area ram_register_area_204 (
    .op(out_194), .x(n4x16_decoder0_1_p5), .bus_in(in), .bus_out(out), .s(s), .e(e), .y(n4x16_decoder1_1_p9));
  RAM_Register_Area ram_register_area_205 (
    .op(out_210), .x(n4x16_decoder0_1_p4), .bus_in(in), .bus_out(out), .s(s), .e(e), .y(n4x16_decoder1_1_p9));
  RAM_Register_Area ram_register_area_206 (
    .op(out_226), .x(n4x16_decoder0_1_p3), .bus_in(in), .bus_out(out), .s(s), .e(e), .y(n4x16_decoder1_1_p9));
  RAM_Register_Area ram_register_area_207 (
    .op(out_242), .x(n4x16_decoder0_1_p2), .bus_in(in), .bus_out(out), .s(s), .e(e), .y(n4x16_decoder1_1_p9));
  RAM_Register_Area ram_register_area_208 (
    .op(out_258), .x(n4x16_decoder0_1_p1), .bus_in(in), .bus_out(out), .s(s), .e(e), .y(n4x16_decoder1_1_p9));
  RAM_Register_Area ram_register_area_209 (
    .op(out_19), .x(n4x16_decoder0_1_p20), .bus_in(in), .bus_out(out), .s(s), .e(e), .y(n4x16_decoder1_1_p8));
  RAM_Register_Area ram_register_area_210 (
    .op(out_35), .x(n4x16_decoder0_1_p19), .bus_in(in), .bus_out(out), .s(s), .e(e), .y(n4x16_decoder1_1_p8));
  RAM_Register_Area ram_register_area_211 (
    .op(out_51), .x(n4x16_decoder0_1_p18), .bus_in(in), .bus_out(out), .s(s), .e(e), .y(n4x16_decoder1_1_p8));
  RAM_Register_Area ram_register_area_212 (
    .op(out_67), .x(n4x16_decoder0_1_p17), .bus_in(in), .bus_out(out), .s(s), .e(e), .y(n4x16_decoder1_1_p8));
  RAM_Register_Area ram_register_area_213 (
    .op(out_83), .x(n4x16_decoder0_1_p15), .bus_in(in), .bus_out(out), .s(s), .e(e), .y(n4x16_decoder1_1_p8));
  RAM_Register_Area ram_register_area_214 (
    .op(out_99), .x(n4x16_decoder0_1_p13), .bus_in(in), .bus_out(out), .s(s), .e(e), .y(n4x16_decoder1_1_p8));
  RAM_Register_Area ram_register_area_215 (
    .op(out_115), .x(n4x16_decoder0_1_p11), .bus_in(in), .bus_out(out), .s(s), .e(e), .y(n4x16_decoder1_1_p8));
  RAM_Register_Area ram_register_area_216 (
    .op(out_131), .x(n4x16_decoder0_1_p9), .bus_in(in), .bus_out(out), .s(s), .e(e), .y(n4x16_decoder1_1_p8));
  RAM_Register_Area ram_register_area_217 (
    .op(out_147), .x(n4x16_decoder0_1_p8), .bus_in(in), .bus_out(out), .s(s), .e(e), .y(n4x16_decoder1_1_p8));
  RAM_Register_Area ram_register_area_218 (
    .op(out_163), .x(n4x16_decoder0_1_p7), .bus_in(in), .bus_out(out), .s(s), .e(e), .y(n4x16_decoder1_1_p8));
  RAM_Register_Area ram_register_area_219 (
    .op(out_179), .x(n4x16_decoder0_1_p6), .bus_in(in), .bus_out(out), .s(s), .e(e), .y(n4x16_decoder1_1_p8));
  RAM_Register_Area ram_register_area_220 (
    .op(out_195), .x(n4x16_decoder0_1_p5), .bus_in(in), .bus_out(out), .s(s), .e(e), .y(n4x16_decoder1_1_p8));
  RAM_Register_Area ram_register_area_221 (
    .op(out_211), .x(n4x16_decoder0_1_p4), .bus_in(in), .bus_out(out), .s(s), .e(e), .y(n4x16_decoder1_1_p8));
  RAM_Register_Area ram_register_area_222 (
    .op(out_227), .x(n4x16_decoder0_1_p3), .bus_in(in), .bus_out(out), .s(s), .e(e), .y(n4x16_decoder1_1_p8));
  RAM_Register_Area ram_register_area_223 (
    .op(out_243), .x(n4x16_decoder0_1_p2), .bus_in(in), .bus_out(out), .s(s), .e(e), .y(n4x16_decoder1_1_p8));
  RAM_Register_Area ram_register_area_224 (
    .op(out_259), .x(n4x16_decoder0_1_p1), .bus_in(in), .bus_out(out), .s(s), .e(e), .y(n4x16_decoder1_1_p8));
  RAM_Register_Area ram_register_area_225 (
    .op(out_20), .x(n4x16_decoder0_1_p20), .bus_in(in), .bus_out(out), .s(s), .e(e), .y(n4x16_decoder1_1_p7));
  RAM_Register_Area ram_register_area_226 (
    .op(out_36), .x(n4x16_decoder0_1_p19), .bus_in(in), .bus_out(out), .s(s), .e(e), .y(n4x16_decoder1_1_p7));
  RAM_Register_Area ram_register_area_227 (
    .op(out_52), .x(n4x16_decoder0_1_p18), .bus_in(in), .bus_out(out), .s(s), .e(e), .y(n4x16_decoder1_1_p7));
  RAM_Register_Area ram_register_area_228 (
    .op(out_68), .x(n4x16_decoder0_1_p17), .bus_in(in), .bus_out(out), .s(s), .e(e), .y(n4x16_decoder1_1_p7));
  RAM_Register_Area ram_register_area_229 (
    .op(out_84), .x(n4x16_decoder0_1_p15), .bus_in(in), .bus_out(out), .s(s), .e(e), .y(n4x16_decoder1_1_p7));
  RAM_Register_Area ram_register_area_230 (
    .op(out_100), .x(n4x16_decoder0_1_p13), .bus_in(in), .bus_out(out), .s(s), .e(e), .y(n4x16_decoder1_1_p7));
  RAM_Register_Area ram_register_area_231 (
    .op(out_116), .x(n4x16_decoder0_1_p11), .bus_in(in), .bus_out(out), .s(s), .e(e), .y(n4x16_decoder1_1_p7));
  RAM_Register_Area ram_register_area_232 (
    .op(out_132), .x(n4x16_decoder0_1_p9), .bus_in(in), .bus_out(out), .s(s), .e(e), .y(n4x16_decoder1_1_p7));
  RAM_Register_Area ram_register_area_233 (
    .op(out_148), .x(n4x16_decoder0_1_p8), .bus_in(in), .bus_out(out), .s(s), .e(e), .y(n4x16_decoder1_1_p7));
  RAM_Register_Area ram_register_area_234 (
    .op(out_164), .x(n4x16_decoder0_1_p7), .bus_in(in), .bus_out(out), .s(s), .e(e), .y(n4x16_decoder1_1_p7));
  RAM_Register_Area ram_register_area_235 (
    .op(out_180), .x(n4x16_decoder0_1_p6), .bus_in(in), .bus_out(out), .s(s), .e(e), .y(n4x16_decoder1_1_p7));
  RAM_Register_Area ram_register_area_236 (
    .op(out_196), .x(n4x16_decoder0_1_p5), .bus_in(in), .bus_out(out), .s(s), .e(e), .y(n4x16_decoder1_1_p7));
  RAM_Register_Area ram_register_area_237 (
    .op(out_212), .x(n4x16_decoder0_1_p4), .bus_in(in), .bus_out(out), .s(s), .e(e), .y(n4x16_decoder1_1_p7));
  RAM_Register_Area ram_register_area_238 (
    .op(out_228), .x(n4x16_decoder0_1_p3), .bus_in(in), .bus_out(out), .s(s), .e(e), .y(n4x16_decoder1_1_p7));
  RAM_Register_Area ram_register_area_239 (
    .op(out_244), .x(n4x16_decoder0_1_p2), .bus_in(in), .bus_out(out), .s(s), .e(e), .y(n4x16_decoder1_1_p7));
  RAM_Register_Area ram_register_area_240 (
    .op(out_260), .x(n4x16_decoder0_1_p1), .bus_in(in), .bus_out(out), .s(s), .e(e), .y(n4x16_decoder1_1_p7));
  RAM_Register_Area ram_register_area_241 (
    .op(out_21), .x(n4x16_decoder0_1_p20), .bus_in(in), .bus_out(out), .s(s), .e(e), .y(n4x16_decoder1_1_p6));
  RAM_Register_Area ram_register_area_242 (
    .op(out_37), .x(n4x16_decoder0_1_p19), .bus_in(in), .bus_out(out), .s(s), .e(e), .y(n4x16_decoder1_1_p6));
  RAM_Register_Area ram_register_area_243 (
    .op(out_53), .x(n4x16_decoder0_1_p18), .bus_in(in), .bus_out(out), .s(s), .e(e), .y(n4x16_decoder1_1_p6));
  RAM_Register_Area ram_register_area_244 (
    .op(out_69), .x(n4x16_decoder0_1_p17), .bus_in(in), .bus_out(out), .s(s), .e(e), .y(n4x16_decoder1_1_p6));
  RAM_Register_Area ram_register_area_245 (
    .op(out_85), .x(n4x16_decoder0_1_p15), .bus_in(in), .bus_out(out), .s(s), .e(e), .y(n4x16_decoder1_1_p6));
  RAM_Register_Area ram_register_area_246 (
    .op(out_101), .x(n4x16_decoder0_1_p13), .bus_in(in), .bus_out(out), .s(s), .e(e), .y(n4x16_decoder1_1_p6));
  RAM_Register_Area ram_register_area_247 (
    .op(out_117), .x(n4x16_decoder0_1_p11), .bus_in(in), .bus_out(out), .s(s), .e(e), .y(n4x16_decoder1_1_p6));
  RAM_Register_Area ram_register_area_248 (
    .op(out_133), .x(n4x16_decoder0_1_p9), .bus_in(in), .bus_out(out), .s(s), .e(e), .y(n4x16_decoder1_1_p6));
  RAM_Register_Area ram_register_area_249 (
    .op(out_149), .x(n4x16_decoder0_1_p8), .bus_in(in), .bus_out(out), .s(s), .e(e), .y(n4x16_decoder1_1_p6));
  RAM_Register_Area ram_register_area_250 (
    .op(out_165), .x(n4x16_decoder0_1_p7), .bus_in(in), .bus_out(out), .s(s), .e(e), .y(n4x16_decoder1_1_p6));
  RAM_Register_Area ram_register_area_251 (
    .op(out_181), .x(n4x16_decoder0_1_p6), .bus_in(in), .bus_out(out), .s(s), .e(e), .y(n4x16_decoder1_1_p6));
  RAM_Register_Area ram_register_area_252 (
    .op(out_197), .x(n4x16_decoder0_1_p5), .bus_in(in), .bus_out(out), .s(s), .e(e), .y(n4x16_decoder1_1_p6));
  RAM_Register_Area ram_register_area_253 (
    .op(out_213), .x(n4x16_decoder0_1_p4), .bus_in(in), .bus_out(out), .s(s), .e(e), .y(n4x16_decoder1_1_p6));
  RAM_Register_Area ram_register_area_254 (
    .op(out_229), .x(n4x16_decoder0_1_p3), .bus_in(in), .bus_out(out), .s(s), .e(e), .y(n4x16_decoder1_1_p6));
  RAM_Register_Area ram_register_area_255 (
    .op(out_245), .x(n4x16_decoder0_1_p2), .bus_in(in), .bus_out(out), .s(s), .e(e), .y(n4x16_decoder1_1_p6));
  RAM_Register_Area ram_register_area_256 (
    .op(out_261), .x(n4x16_decoder0_1_p1), .bus_in(in), .bus_out(out), .s(s), .e(e), .y(n4x16_decoder1_1_p6));
endmodule

module Register (
  input  [7:0] i,
  input  s,
  input  e,
  output [7:0] o
);

  wire [7:0] n1_byte_memory_1_o;

  _1_byte_Memory u_1_byte_memory_1 (.o(n1_byte_memory_1_o), .i(i), .s(s));
  _1_byte_Enabler u_1_byte_enabler_1 (.o(i), .i(n1_byte_memory_1_o), .e(e));

  assign o = i;
endmodule
