// Logisim project CPU_BasicGates.circ as structural Verilog: 5 circuits, main circuit NOT
module NOT (
  input  s,
  output o
);

  nand nand_1 (o, s, s);
endmodule

module AND (
  input  a,
  input  b,
  output o
);

  wire nand_1_out;

  nand nand_1 (nand_1_out, a, b);
  NOT not_1 (.o(o), .s(nand_1_out));
endmodule

module OR (
  input  a,
  input  b,
  output c
);

  wire not_1_out, not_2_out;

  not not_1 (not_1_out, a);
  not not_2 (not_2_out, b);
  nand nand_1 (c, not_1_out, not_2_out);
endmodule

module XOR (
  input  a,
  input  b,
  output c
);

  wire nand_1_out, nand_2_out, not_1_out, not_2_out;

  not not_1 (not_1_out, a);
  not not_2 (not_2_out, b);
  nand nand_1 (nand_1_out, not_1_out, b);
  nand nand_2 (nand_2_out, a, not_2_out);
  nand nand_3 (c, nand_1_out, nand_2_out);
endmodule

module _3_And (
  input  a,
  input  b,
  input  c,
  output o
);

  wire and_1_out;

  and and_1 (and_1_out, a, b);
  and and_2 (o, and_1_out, c);
endmodule
