// Logisim project CPU_Memory.circ as structural Verilog: 5 circuits, main circuit 1 bit Memory
module _1_bit_Memory (
  input  i,
  input  s,
  output o
);

  wire nand_1_out, nand_2_out, nand_4_out;

  nand nand_1 (nand_1_out, i, s);
  nand nand_2 (nand_2_out, nand_1_out, s);
  nand nand_3 (o, nand_1_out, nand_4_out);
  nand nand_4 (nand_4_out, o, nand_2_out);
endmodule

module _8_bit_Memory (
  input  i,
  input  i_2,
  input  i_3,
  input  i_4,
  input  i_5,
  input  i_6,
  input  i_7,
  input  i_8,
  input  s,
  output o,
  output o_2,
  output o_3,
  output o_4,
  output o_5,
  output o_6,
  output o_7,
  output o_8
);

  _1_bit_Memory u_1_bit_memory_1 (.o(o), .i(i), .s(s));
  _1_bit_Memory u_1_bit_memory_2 (.o(o_2), .i(i_2), .s(s));
  _1_bit_Memory u_1_bit_memory_3 (.o(o_3), .i(i_3), .s(s));
  _1_bit_Memory u_1_bit_memory_4 (.o(o_4), .i(i_4), .s(s));
  _1_bit_Memory u_1_bit_memory_5 (.o(o_5), .i(i_5), .s(s));
  _1_bit_Memory u_1_bit_memory_6 (.o(o_6), .i(i_6), .s(s));
  _1_bit_Memory u_1_bit_memory_7 (.o(o_7), .i(i_7), .s(s));
  _1_bit_Memory u_1_bit_memory_8 (.o(o_8), .i(i_8), .s(s));
endmodule

module _1_byte_Memory (
  input  [7:0] i,
  input  s,
  output [7:0] o
);

  _1_bit_Memory u_1_bit_memory_1 (.o(o[7]), .i(i[7]), .s(s));
  _1_bit_Memory u_1_bit_memory_2 (.o(o[6]), .i(i[6]), .s(s));
  _1_bit_Memory u_1_bit_memory_3 (.o(o[5]), .i(i[5]), .s(s));
  _1_bit_Memory u_1_bit_memory_4 (.o(o[4]), .i(i[4]), .s(s));
  _1_bit_Memory u_1_bit_memory_5 (.o(o[3]), .i(i[3]), .s(s));
  _1_bit_Memory u_1_bit_memory_6 (.o(o[2]), .i(i[2]), .s(s));
  _1_bit_Memory u_1_bit_memory_7 (.o(o[1]), .i(i[1]), .s(s));
  _1_bit_Memory u_1_bit_memory_8 (.o(o[0]), .i(i[0]), .s(s));
endmodule

module _8_bit_Enabler (
  input  i,
  input  i_2,
  input  i_3,
  input  i_4,
  input  i_5,
  input  i_6,
  input  i_7,
  input  i_8,
  input  e,
  output o,
  output o_2,
  output o_3,
  output o_4,
  output o_5,
  output o_6,
  output o_7,
  output o_8
);

  and and_1 (o, i, e);
  and and_2 (o_2, i_2, e);
  and and_3 (o_3, i_3, e);
  and and_4 (o_4, i_4, e);
  and and_5 (o_5, i_5, e);
  and and_6 (o_6, i_6, e);
  and and_7 (o_7, i_7, e);
  and and_8 (o_8, i_8, e);
endmodule

module _1_byte_Enabler (
  input  [7:0] i,
  input  e,
  output [7:0] o
);

  and and_1 (o[7], i[7], e);
  and and_2 (o[6], i[6], e);
  and and_3 (o[5], i[5], e);
  and and_4 (o[4], i[4], e);
  and and_5 (o[3], i[3], e);
  and and_6 (o[2], i[2], e);
  and and_7 (o[1], i[1], e);
  and and_8 (o[0], i[0], e);
endmodule
